# Fritzing sketch 7_1 (saved by Fritzing 0.9.3b)
breadboards: 1

parts:
  U1 = MLX90614 [package=to-39]  # not connected
  R1 = Resistor [tolerance=±5% resistance=220 package=THT]
  LED1 = LED - 5mm [color="Red (633nm)" package="5 mm [THT]"]  # not connected
  Raspberry_Pi_1 = Raspberry Pi 3 [part_number=RPI-3-V1.2]

nets:
  N1: R1.Pin_0, Raspberry_Pi_1.GND
