# Fritzing sketch safe_traffic (saved by Fritzing 0.9.3b)
breadboards: 1

parts:
  Raspberry_Pi_1 = Raspberry Pi 3 [part_number=RPI-3-V1.2]
  S1 = Momentary Switch [package=ksa_sealed_tac_switch]
  LED1 = smd LED [color="Red (633nm)" package="1206 [SMD]"]
  LED2 = smd LED [color="Red (633nm)" package="1206 [SMD]"]
  U1 = MLX90614 [package=to-39]  # not connected
  J1 = Basic Servo  # not connected
  R1 = Resistor [tolerance=±5% resistance=220 package=THT]
  R2 = Resistor [tolerance=±5% resistance=220 package=THT]
  R3 = Resistor [tolerance=±5% resistance=220 package=THT]

nets:
  N1: Raspberry_Pi_1.3v3, R3.Pin_1
  N2: Raspberry_Pi_1.GND, R1.Pin_0, R2.Pin_0
  N3: Raspberry_Pi_1.GIPO21, LED1.anode
  N4: Raspberry_Pi_1.GIPO16, LED2.anode
  N5: S1.4, R3.Pin_0
  N6: LED1.cathode, R1.Pin_1
  N7: LED2.cathode, R2.Pin_1
