# Fritzing sketch 7_2 (saved by Fritzing 0.9.3b)
breadboards: 1

parts:
  Raspberry_Pi_1 = Raspberry Pi 3 [part_number=RPI-3-V1.2]
  R1 = Resistor [tolerance=±5% resistance=220 package=THT]
  LED1 = LED - 5mm [color="Red (633nm)" package="5 mm [THT]"]
  hc-sr1 = hc-sr04

nets:
  N1: Raspberry_Pi_1.GPIO19, hc-sr1.Echo
  N2: Raspberry_Pi_1.GPIO26, hc-sr1.Trig
  N3: Raspberry_Pi_1.GPIO21, LED1.anode
  N4: Raspberry_Pi_1.GPIO20, hc-sr1.GND
  N5: Raspberry_Pi_1.GND, R1.Pin_0
  5V: Raspberry_Pi_1.5V, hc-sr1.VCC
  N6: R1.Pin_1, LED1.cathode
